# Fritzing sketch CameraShield (saved by Fritzing 0.7.11b)
breadboards: 1

parts:
  J3 = female pin header, 2 pins [form="♀ (female)"]
  J1 = female pin header, 8 pins [form="♀ (female)"]
  J2 = female pin header, 4 pins [form="♀ (female)"]
  Arduino_Ethernet_Shield1 = Arduino Ethernet Shield

nets:
  N1: J3.pin1, J2.pin4
  N2: J3.pin2, J2.pin3
  N3: J1.pin1, J1.pin3, J1.pin4, J1.pin8, J2.pin2, Arduino_Ethernet_Shield1.GND
  N4: J1.pin2, J1.pin6, Arduino_Ethernet_Shield1.3V3
  N5: J1.pin5, Arduino_Ethernet_Shield1.D8
  N6: J1.pin7, Arduino_Ethernet_Shield1.D7
  N7: J2.pin1, Arduino_Ethernet_Shield1.+5V

notes:
  WARNING! This board is the older Ethernet Shield. We need it with the R3 pinouts.
