# Fritzing sketch OAP_Zigbee_Controller (saved by Fritzing 0.7.11b)
breadboards: 1

parts:
  U1 = XBee
  Arduino1 = Arduino Mega

nets:
  VCC: U1.VCC, Arduino1.3V3
  N1: U1.pin2, Arduino1.D17
  N2: U1.pin3, Arduino1.D16
  GND: U1.GND, Arduino1.GND

notes:
  Configure THIS radio as a "ZigBee Coordinator API"
  You will need X-CTU to do this
  ATID - PAN - ATID2445
  Ensure API mode is OFF / DISABLED!
  ATWR
  See www.oneassetplace.com for more directions
