# Fritzing sketch OAP_Zigbee_Remote_Sensor (saved by Fritzing 0.7.11b)
breadboards: 1

parts:
  U1 = XBee
  R1 = Photocell (LDR) [part_number="1K Light, 10K Dark" package=THT]
  R2 = Resistor [tolerance=±5% resistance=15k part_number="18k " package=THT]
  U2 = Voltage Regulator - 3.3V [part_number=LD1117V33 package="TO220 [THT]"]  # not connected
  T1 = LM35 Temperature Sensor [part_number=LM335 package="TO92 [THT]"]
  R3 = Resistor [tolerance=±5% resistance=330 part_number="300 ohm" package=THT]
  R4 = Resistor [tolerance=±5% resistance=220 package=THT]
  R5 = Resistor [tolerance=±5% resistance=100k package=THT]
  S1 = Toggle Switch [package=THT]
  R6 = Resistor [tolerance=±5% resistance=10k package=THT]

nets:
  N1: U1.VCC, R2.Pin_1, R3.Pin_1, S1.L1
  GND: U1.GND, R1.pin_0, T1.GND, R5.Pin_0, R6.Pin_0
  N2: U1.pin18, S1.COM, R6.Pin_1
  N3: U1.pin19, R1.pin_1, R2.Pin_0
  N4: U1.pin20, R4.Pin_0, R5.Pin_1
  N5: T1.Vout, R3.Pin_0, R4.Pin_1

notes:
  Use LD1117v33 and two capacitors to take 9v input to 3.3v
  ATID - PAN - ATID2445
  AD0 (20) - Analog Input - ATD02
  AD1 (19) - Analog Input - ATD12
  AD2 (18) - Digital Input - ATD23
  60 Sec = 0x7530= ATIR7530
  ATWR
  See www.oneassetplace for more directions
